# Fritzing sketch Circuit Diagram (saved by Fritzing 0.9.4)
breadboards: 1

parts:
  Part2 = HX711 Weighing Sensor Module
  Tare = Pushbutton [package=THT]
  LCD1 = LCD screen
  R2 = Resistor [tolerance=±5% resistance=220 package="1206 [SMD]"]
  IC1 = IC, SIP package, 4 pins [chip_label=TAL220]
  Part1 = Arduino Nano (Rev3.0)
  R1_10k = TRIMPOT [package=trimpot_tc33]

nets:
  N1: Part2.VCC, Part1.D4
  GND: Part2.GND, Tare.leg1, LCD1.VSS, LCD1.R/W, LCD1.LED-, Part1.GND, R1_10k.CCW
  N2: Part2.DO/RX, Part1.D2
  N3: Part2.CK/TX, Part1.D3
  N4: Part2.E+, IC1.pin4
  N5: Part2.E-, IC1.pin3
  N6: Part2.A+, IC1.pin2
  N7: Part2.A-, IC1.pin1
  N8: Tare.leg0, Part1.D8
  N9: LCD1.VDD, R2.Pin_0, Part1.D5, R1_10k.CW
  N10: LCD1.V0, R1_10k.WIPER
  N11: LCD1.RS, Part1.A0
  N12: LCD1.E, Part1.A1
  N13: LCD1.DB4, Part1.A2
  N14: LCD1.DB5, Part1.A3
  N15: LCD1.DB6, Part1.A4
  N16: LCD1.DB7, Part1.A5
  N17: LCD1.LED+, R2.Pin_1
